// Logisim project LC-3.circ as structural Verilog: 14 circuits, main circuit main
module main (
  input  Reset,
  output out_2,
  output out_3,
  output out_4,
  output out_5,
  output out_6,
  output out_7,
  output out_8,
  output out_9,
  output [15:0] out_10,
  output [15:0] out_11,
  output [15:0] out_12,
  output [15:0] out_13,
  output [15:0] out_14,
  output [15:0] out_15,
  output [15:0] out_16,
  output [15:0] out_17,
  output [15:0] out_18,
  output halt,
  output [15:0] out_20,
  output [15:0] out_21,
  output [15:0] out_22,
  output [15:0] out_23
);

  wire and_2_out, Arith, cond_LDI, decodeir_1_jsr_jsrr, decodeir_1_writereg, fin_cond_LDI,
       getaddr_1_garde_pc, getcst_1_usecst, LDI_STI, or16_1_out_2, or16_2_out_2, ramctrl_1_memload,
       ramctrl_1_memstore, STI, WriteR7;
  wire [3:0] nzp_1_nzpo;
  wire [15:0] getcst_1_cst, ram_1_data, RegIN, registres_1_out_sr1, registres_1_out_sr2, RES;

  RegPC regpc_1 (
    .IR(out_11), .R(registres_1_out_sr1), .TestNZP(out_5), .PC(out_10), .Jump(out_4), .H(out_3),
    .Reset(Reset), .change_PC_LDI(getaddr_1_garde_pc));
  BiClock biclock_1 (.reset(Reset), .signal0(out_2), .signal1(out_3));
  // Probe on out_10
  GetAddr getaddr_1 (
    .PC(out_10), .IR(out_11), .Addr(out_12), .Fetch(out_2), .R(registres_1_out_sr1), .MemOUT(ram_1_data),
    .LDI_STI(LDI_STI), .Exec(out_3), .fin_cond_LDI_STI(fin_cond_LDI), .cond_LDI_STI(cond_LDI),
    .garde_PC(getaddr_1_garde_pc));
  // Probe on out_12
  // Probe on out_13
  RamCtrl ramctrl_1 (
    .Store(out_7), .Fetch(out_2), .Exec(out_3), .Load(out_6), .MemStore(ramctrl_1_memstore),
    .MemLoad(ramctrl_1_memload), .STI(STI));
  // Probe on ram_1_data
  RAM #(.addrWidth(16), .dataWidth(16), .bus("separate")) ram_1 (
    .addr(out_12), .din(out_13), .data(ram_1_data), .str(ramctrl_1_memstore), .clk(ramctrl_1_memstore),
    .ld(ramctrl_1_memload));  // open: sel, clr
  LED led_1 (.in(out_6));
  LED led_2 (.in(out_7));
  and and_1 (WriteR7, decodeir_1_jsr_jsrr, out_3);
  RegIN regin_1 (.PC(out_10), .IR(out_11), .MemOUT(ram_1_data), .Fetch(out_2), .RES(RES), .RegIN(RegIN));
  Register #(.width(16), .trigger("falling")) register_1 (
    .D(ram_1_data), .Q(out_11), .clk(and_2_out), .clr(fin_cond_LDI));  // open: en
  and and_2 (and_2_out, out_2, ~cond_LDI);  // AND_Gate
  DecodeIR decodeir_1 (
    .IR(out_11), .Jump(out_4), .WriteReg(decodeir_1_writereg), .Load(out_6), .Store(out_7), .Arith(Arith),
    .JSR_JSRR(decodeir_1_jsr_jsrr), .LDI_STI(LDI_STI), .STI(STI));
  // Probe on out_11[11:9]
  Registres registres_1 (
    .SR1(out_11[8:6]), .IN(RegIN), .SR2(out_11[2:0]), .DR_SR(out_11[11:9]), .OUT_SR1(registres_1_out_sr1),
    .OUT_SR2(registres_1_out_sr2), .OUT_SR(out_13), .R0(out_15), .R1(out_16), .R2(out_17), .R3(out_18),
    .R4(out_20), .R5(out_21), .R6(out_22), .R7(out_23), .WriteReg(out_8), .WriteR7(WriteR7));
  // Probe on out_11[8:6]
  // Probe on out_11[2:0]
  // Probe on registres_1_out_sr1
  ALU alu_1 (
    .UseCst(getcst_1_usecst), .e2(out_11[15:14]), .Input1(registres_1_out_sr1), .Input2(registres_1_out_sr2),
    .Cst(getcst_1_cst), .Output(RES), .overflow(out_9), .Arith(Arith));
  // Probe on getcst_1_cst
  GetCst getcst_1 (.IR(out_11), .Cst(getcst_1_cst), .UseCst(getcst_1_usecst));
  // Probe on out_11[15:14]
  and and_3 (out_8, decodeir_1_writereg, out_3);
  // Probe on registres_1_out_sr2
  NZP nzp_1 (
    .RegIN(RegIN), .NZPO(nzp_1_nzpo), .IR(out_11), .TestNZP(out_5), .WriteReg(out_8), .overflow(out_9));  // open: NZP_IR
  Or16 or16_1 (.in_1(out_11), .out_2(or16_1_out_2));
  and and_4 (halt, ~or16_1_out_2, or16_2_out_2);  // AND_Gate
  Or16 or16_2 (.in_1(out_10), .out_2(or16_2_out_2));
  // Probe on out_15
  // Probe on out_16
  // Probe on out_17
  // Probe on out_18
  // Probe on out_20
  // Probe on out_21
  // Probe on out_22
  // Probe on out_23
  // Probe on RES
  // Probe on nzp_1_nzpo

  // Other names for the same wires on the sheet: Addr[15:0] = out_12; Condition = out_5; Exec = out_3; Fetch = out_2;
  //   IR[15:0] = out_11; JumpInstr = out_4; Load = out_6; MemIN[15:0] = out_13; MemOUT[15:0] = out_14;
  //   overflow = out_9; PC[15:0] = out_10; R0[15:0] = out_15; R1[15:0] = out_16; R2[15:0] = out_17; R3[15:0] = out_18;
  //   R4[15:0] = out_20; R5[15:0] = out_21; R6[15:0] = out_22; R7[15:0] = out_23; Store = out_7; WriteReg = out_8

  // Notes on the sheet:
  //   R
  //   IR
  //   PC
  //   R
  //   IR
  //   GetRegs
  //   GetOp
endmodule

module ALU (
  input  [15:0] Input1,
  input  [15:0] Input2,
  input  [15:0] Cst,
  input  UseCst,
  input  Arith,
  input  [1:0] e2,
  output overflow,
  output [15:0] Output
);

  wire adder_1_cout;
  wire [15:0] adder_1_out, and_2_out, multiplexer_1_out, not_1_out;

  Multiplexer #(.width(16), .enable("false")) multiplexer_1 (
    .in0(Input2), .in1(Cst), .out(multiplexer_1_out), .sel(UseCst));
  and and_1 (overflow, Arith, adder_1_cout);
  Adder #(.width(16)) adder_1 (.a(multiplexer_1_out), .b(Input1), .out(adder_1_out), .cout(adder_1_cout));  // open: cin
  assign and_2_out = Input1 & multiplexer_1_out;  // AND_Gate and_2, 16 bits wide
  Multiplexer #(.select(2), .width(16), .enable("false")) multiplexer_2 (
    .in0(adder_1_out), .in1(and_2_out), .in2(not_1_out), .in3(adder_1_out), .out(Output), .sel(e2));
  assign not_1_out = ~Input1;  // NOT_Gate not_1, 16 bits wide

  // Notes on the sheet:
  //   Peut poser probleme avec commande JMP
endmodule

module BiClock (
  input  reset,
  output signal0,
  output signal1
);

  wire and_1_out, horloge_out, not_1_out, register_1_q;

  Clock horloge (.out(horloge_out));
  not not_1 (not_1_out, register_1_q);
  Register #(.width(1), .trigger("falling")) register_1 (
    .D(not_1_out), .Q(register_1_q), .clk(horloge_out), .clr(reset));  // open: en
  and and_1 (and_1_out, horloge_out, ~reset);  // AND_Gate
  and and_2 (signal0, ~register_1_q, and_1_out);  // AND_Gate
  and and_3 (signal1, register_1_q, and_1_out);

  // Notes on the sheet:
  //   Ce module divise une horloge en deux sous-horloges alternées
  //   Chronogrammes :
  //   horloge: 0101010101 signal0: 0100010001 signal1: 000100010
  //   registre 1-bit
  //   Enable
  //   select : 0 / 1
endmodule

module DecodeIR (
  input  [15:0] IR,
  output JSR_JSRR,
  output STI,
  output LDI_STI,
  output Jump,
  output Arith,
  output Load,
  output Store,
  output WriteReg
);

  wire decoder_1_out1, decoder_1_out2, or_1_out;

  Decoder #(.select(2), .enable("false")) decoder_1 (
    .out1(decoder_1_out1), .out2(decoder_1_out2), .sel(IR[15:14]));  // open: out0, out3
  Decoder #(.select(2), .enable("false")) decoder_2 (
    .out0(Jump), .out1(Arith), .out2(Load), .out3(Store), .sel(IR[13:12]));
  and and_1 (JSR_JSRR, decoder_1_out1, Jump);
  or or_1 (or_1_out, Store, Load);
  or or_2 (WriteReg, Arith, Load);
  and and_2 (STI, decoder_1_out2, Store);
  and and_3 (LDI_STI, decoder_1_out2, or_1_out);
endmodule

module GetAddr (
  input  [15:0] PC,
  input  Fetch,
  input  Exec,
  input  [15:0] IR,
  input  [15:0] R,
  input  LDI_STI,
  input  [15:0] MemOUT,
  output [15:0] Addr,
  output fin_cond_LDI_STI,
  output cond_LDI_STI,
  output garde_PC
);

  wire and_1_out, and_3_out, comparator_1_eq, Reset;
  wire [7:0] counter_1_q;
  wire [15:0] adder_4_out, Addr_LDI, Addr_LDI_STI, LD_ST, LDR_STR, multiplexer_1_out, multiplexer_2_out,
       multiplexer_3_out, multiplexer_4_out, offset6_1_off6, offset9_1_off9, offset9_2_off9, PC_1;

  Offset6 offset6_1 (.IR(IR), .Off6(offset6_1_off6));
  Adder #(.width(16)) adder_1 (.a(PC), .b({16{1'b0}}), .out(PC_1), .cin(1'b1));  // open: cout
  Offset9 offset9_1 (.IR(IR), .Off9(offset9_1_off9));
  Adder #(.width(16)) adder_2 (.a(R), .b(offset6_1_off6), .out(LDR_STR));  // open: cin, cout
  Offset9 offset9_2 (.IR(MemOUT), .Off9(offset9_2_off9));
  // Probe on LD_ST
  Adder #(.width(16)) adder_3 (.a(offset9_1_off9), .b(PC_1), .out(LD_ST));  // open: cin, cout
  // Probe on adder_4_out
  Adder #(.width(16)) adder_4 (.a(offset9_2_off9), .b(PC_1), .out(adder_4_out));  // open: cin, cout
  Counter counter_1 (.Q(counter_1_q), .clk(Exec), .clr(Reset));  // open: load, D, count, carry
  Multiplexer #(.width(16), .enable("false")) multiplexer_1 (
    .in0(adder_4_out), .in1(MemOUT), .out(multiplexer_1_out), .sel(LDI_STI));
  Multiplexer #(.select(2), .width(16), .enable("false")) multiplexer_2 (
    .in0(LD_ST), .in1(LDR_STR), .in2(Addr_LDI), .in3(PC), .out(multiplexer_2_out), .sel(IR[15:14]));
  Register #(.width(16)) register_1 (
    .D(multiplexer_1_out), .Q(Addr_LDI_STI), .clk(and_1_out), .clr(Reset));  // open: en
  and and_1 (and_1_out, ~Exec, ~Fetch);  // AND_Gate
  Comparator comparator_1 (.a(counter_1_q), .b(8'h1), .gt(fin_cond_LDI_STI), .eq(comparator_1_eq));  // open: lt
  Multiplexer #(.select(2), .width(16), .enable("false")) multiplexer_3 (
    .in0(PC), .in1(PC), .in2(multiplexer_2_out), .in3(multiplexer_2_out), .out(multiplexer_3_out),
    .sel(IR[13:12]));
  and and_2 (cond_LDI_STI, ~fin_cond_LDI_STI, LDI_STI);  // AND_Gate
  and and_3 (and_3_out, comparator_1_eq, Exec);
  and and_4 (Reset, Fetch, ~LDI_STI);  // AND_Gate
  and and_5 (garde_PC, cond_LDI_STI, and_3_out);
  Multiplexer #(.width(16), .enable("false")) multiplexer_4 (
    .in0(multiplexer_3_out), .in1(PC), .out(multiplexer_4_out), .sel(Fetch));
  Multiplexer #(.width(16), .enable("false")) multiplexer_5 (
    .in0(multiplexer_4_out), .in1(Addr_LDI_STI), .out(Addr), .sel(cond_LDI_STI));

  // Notes on the sheet:
  //   LD/ST
  //   LDR/STR
  //   TRAP
  //   Store/Load
  //   Permet de réinitialiser l'addr
endmodule

module GetCst (
  input  [15:0] IR,
  output [15:0] Cst,
  output UseCst
);

  assign Cst = {{11{IR[4]}}, IR[4:0]};  // Bit_Extender bit_extender_1

  assign UseCst = IR[5];
endmodule

// NZPO
module NZP (
  input  overflow,
  input  [15:0] RegIN,
  input  WriteReg,
  input  [15:0] IR,
  output [3:0] NZPO,
  output TestNZP,
  output [2:0] NZP_IR
);

  wire not_1_out, or16_1_out_2;
  wire [2:0] and_2_out;
  wire [2:1] and_1_out;

  Or16 or16_1 (.in_1(RegIN), .out_2(or16_1_out_2));
  not not_1 (not_1_out, RegIN[15]);
  and and_1 (and_1_out[1], not_1_out, or16_1_out_2);
  not not_2 (and_1_out[2], or16_1_out_2);
  Register #(.width(4), .trigger("falling")) Reg_NZPO (
    .D({RegIN[15], and_1_out, overflow}), .Q(NZPO), .clk(WriteReg));  // open: en, clr
  assign and_2_out = NZPO[3:1] & IR[11:9];  // AND_Gate and_2, 3 bits wide
  or or_1 (TestNZP, and_2_out[0], and_2_out[1], and_2_out[2]);

  assign NZP_IR = IR[11:9];

  // Notes on the sheet:
  //   pos
  //   zero
  //   neg
  //   Test de saut
endmodule

// Off6
module Offset6 (
  input  [15:0] IR,
  output [15:0] Off6
);

  assign Off6 = {{10{IR[5]}}, IR[5:0]};  // Bit_Extender bit_extender_1
endmodule

// Off9
module Offset9 (
  input  [15:0] IR,
  output [15:0] Off9
);

  assign Off9 = {{7{IR[8]}}, IR[8:0]};  // Bit_Extender bit_extender_1
endmodule

module Or16 (
  input  [15:0] in_1,
  output out_2
);

  wire [3:0] or_1_out;

  assign or_1_out = in_1[3:0] | in_1[7:4] | in_1[11:8] | in_1[15:12];  // OR_Gate or_1, 4 bits wide
  or or_2 (out_2, or_1_out[0], or_1_out[1], or_1_out[2], or_1_out[3]);
endmodule

module RamCtrl (
  input  Exec,
  input  Fetch,
  input  Load,
  input  Store,
  input  STI,
  output MemLoad,
  output MemStore
);

  wire and_1_out, and_2_out, or_1_out;

  and and_1 (and_1_out, Exec, Load);
  and and_2 (and_2_out, Exec, Store);
  or or_1 (or_1_out, Fetch, and_1_out);
  Multiplexer #(.enable("false")) multiplexer_1 (.in0(or_1_out), .in1(and_2_out), .out(MemLoad), .sel(STI));
  Multiplexer #(.enable("false")) multiplexer_2 (.in0(and_2_out), .in1(or_1_out), .out(MemStore), .sel(STI));

  // Notes on the sheet:
  //   On inverse les valeurs de MemLoad et MemStore quand STI est activé
endmodule

module Registres (
  input  [2:0] SR1,
  input  [15:0] IN,
  input  [2:0] SR2,
  input  [2:0] DR_SR,
  input  WriteReg,
  input  WriteR7,
  output [15:0] R0,
  output [15:0] OUT_SR1,
  output [15:0] R1,
  output [15:0] R2,
  output [15:0] R3,
  output [15:0] OUT_SR2,
  output [15:0] R4,
  output [15:0] R5,
  output [15:0] OUT_SR,
  output [15:0] R6,
  output [15:0] R7
);

  wire decoder_1_out0, decoder_1_out1, decoder_1_out2, decoder_1_out3, decoder_1_out4, decoder_1_out5,
       decoder_1_out6, decoder_1_out7, or_1_out;

  Decoder #(.select(3), .disabled(0)) decoder_1 (
    .out0(decoder_1_out0), .out1(decoder_1_out1), .out2(decoder_1_out2), .out3(decoder_1_out3),
    .out4(decoder_1_out4), .out5(decoder_1_out5), .out6(decoder_1_out6), .out7(decoder_1_out7), .sel(DR_SR),
    .en(WriteReg));
  or or_1 (or_1_out, WriteR7, decoder_1_out7);
  Register #(.width(16), .trigger("falling")) u_R0 (.D(IN), .Q(R0), .clk(decoder_1_out0));  // open: en, clr
  Register #(.width(16), .trigger("falling")) u_R1 (.D(IN), .Q(R1), .clk(decoder_1_out1));  // open: en, clr
  Register #(.width(16), .trigger("falling")) u_R2 (.D(IN), .Q(R2), .clk(decoder_1_out2));  // open: en, clr
  Register #(.width(16), .trigger("falling")) u_R3 (.D(IN), .Q(R3), .clk(decoder_1_out3));  // open: en, clr
  Register #(.width(16), .trigger("falling")) u_R4 (.D(IN), .Q(R4), .clk(decoder_1_out4));  // open: en, clr
  Register #(.width(16), .trigger("falling")) u_R5 (.D(IN), .Q(R5), .clk(decoder_1_out5));  // open: en, clr
  Register #(.width(16), .trigger("falling")) u_R6 (.D(IN), .Q(R6), .clk(decoder_1_out6));  // open: en, clr
  Register #(.width(16), .trigger("falling")) u_R7 (.D(IN), .Q(R7), .clk(or_1_out));  // open: en, clr
  Multiplexer #(.select(3), .width(16), .enable("false")) multiplexer_1 (
    .in0(R0), .in1(R1), .in2(R2), .in3(R3), .in4(R4), .in5(R5), .in6(R6), .in7(R7), .out(OUT_SR1), .sel(SR1));
  Multiplexer #(.select(3), .width(16), .enable("false")) multiplexer_2 (
    .in0(R0), .in1(R1), .in2(R2), .in3(R3), .in4(R4), .in5(R5), .in6(R6), .in7(R7), .out(OUT_SR2), .sel(SR2));
  Multiplexer #(.select(3), .width(16), .enable("false")) multiplexer_3 (
    .in0(R0), .in1(R1), .in2(R2), .in3(R3), .in4(R4), .in5(R5), .in6(R6), .in7(R7), .out(OUT_SR), .sel(DR_SR));
endmodule

module RegPC (
  input  change_PC_LDI,
  input  Jump,
  input  H,
  input  Reset,
  input  TestNZP,
  input  [15:0] IR,
  input  [15:0] R,
  output [15:0] PC
);

  wire [15:0] adder_2_out, adder_3_out, bit_extender_1_out, multiplexer_1_out, multiplexer_2_out,
       multiplexer_3_out, multiplexer_4_out, offset9_1_off9, PC_1, PCJumped;

  Adder #(.width(16)) adder_1 (.a(PC), .b({16{1'b0}}), .out(PC_1), .cin(1'b1));  // open: cout
  Offset9 offset9_1 (.IR(IR), .Off9(offset9_1_off9));
  assign bit_extender_1_out = {{5{IR[10]}}, IR[10:0]};  // Bit_Extender bit_extender_1
  Multiplexer #(.width(16), .enable("false")) multiplexer_1 (
    .in0(PC_1), .in1(PCJumped), .out(multiplexer_1_out), .sel(Jump));
  Adder #(.width(16)) adder_2 (.a(PC_1), .b(offset9_1_off9), .out(adder_2_out));  // open: cin, cout
  Adder #(.width(16)) adder_3 (.a(PC_1), .b(bit_extender_1_out), .out(adder_3_out));  // open: cin, cout
  Multiplexer #(.width(16), .enable("false")) multiplexer_2 (
    .in0(multiplexer_1_out), .in1(PC), .out(multiplexer_2_out), .sel(change_PC_LDI));
  // Probe on multiplexer_2_out
  Multiplexer #(.width(16), .enable("false")) multiplexer_3 (
    .in0(PC_1), .in1(adder_2_out), .out(multiplexer_3_out), .sel(TestNZP));
  Multiplexer #(.width(16), .enable("false")) multiplexer_4 (
    .in0(R), .in1(adder_3_out), .out(multiplexer_4_out), .sel(IR[11]));
  Register #(.width(16), .trigger("falling")) u_PC (.D(multiplexer_2_out), .Q(PC), .clk(H), .clr(Reset));  // open: en
  Multiplexer #(.select(2), .width(16), .enable("false")) multiplexer_5 (
    .in0(multiplexer_3_out), .in1(multiplexer_4_out), .in2(PC_1), .in3(R), .out(PCJumped), .sel(IR[15:14]));

  // Other names for the same wires on the sheet: JMP[15:0] = R

  // Notes on the sheet:
  //   NOP
  //   BR
  //   JSRR
  //   JSR
  //   Choix du Jump
  //   RTI(Non implémenté)
endmodule

module RegIN (
  input  [15:0] PC,
  input  [15:0] RES,
  input  [15:0] MemOUT,
  input  Fetch,
  input  [15:0] IR,
  output [15:0] RegIN
);

  wire [15:0] adder_2_out, multiplexer_1_out, multiplexer_2_out, offset9_1_off9, PC_1, register_1_q;

  Register #(.width(16), .trigger("falling")) register_1 (.D(MemOUT), .Q(register_1_q), .clk(Fetch));  // open: en, clr
  Offset9 offset9_1 (.IR(IR), .Off9(offset9_1_off9));
  Adder #(.width(16)) adder_1 (.a(PC), .b({16{1'b0}}), .out(PC_1), .cin(1'b1));  // open: cout
  Adder #(.width(16)) adder_2 (.a(PC_1), .b(offset9_1_off9), .out(adder_2_out));  // open: cin, cout
  // Probe on adder_2_out
  // Probe on PC_1
  Multiplexer #(.select(2), .width(16), .enable("false")) multiplexer_1 (
    .in0(MemOUT), .in1(MemOUT), .in2(register_1_q), .in3(adder_2_out), .out(multiplexer_1_out),
    .sel(IR[15:14]));
  // Probe on IR[15:14]
  // Probe on RES
  // Probe on multiplexer_1_out
  Multiplexer #(.select(2), .width(16), .enable("false")) multiplexer_2 (
    .in1(PC_1), .out(multiplexer_2_out), .sel(IR[15:14]));  // open: in0, in2, in3
  Multiplexer #(.select(2), .width(16), .enable("false")) multiplexer_3 (
    .in0(multiplexer_2_out), .in1(RES), .in2(multiplexer_1_out), .out(RegIN), .sel(IR[13:12]));  // open: in3
  // Probe on RegIN

  // Notes on the sheet:
  //   LDI
  //   LD/LDR
  //   LEA
  //   PC+1
  //   (STR)
  //   JSR/JSRR
  //   Arith
  //   Load
endmodule
